// Logisim project projeto.circ as structural Verilog: 9 circuits, main circuit aritmetica
module main (
  input  [7:0] A,
  input  [7:0] B,
  input  s,
  output f0__Overflow,
  output f1__A___B,
  output f2__A___B,
  output f3__A___B,
  output [7:0] R
);

  ULA ula_1 (.overflow(f0__Overflow), .f1(f1__A___B), .f2(f2__A___B), .f3(f3__A___B), .A(A), .p(s), .B(B), .R(R));

  // Notes on the sheet:
  //   Arthur Massola 10297904
  //   Aurea Hariki: 9298594 
  //   Bruna Thalenberg: 8569211
  //   s: pino seletor
  //   0 para soma
  //   f0: flag de overflow
  //   Projeto de Álgebra Booleana
  //   A, B: bytes de entrada
  //   R: byte resultado (saída)
  //   1 para subtração
  //   ULA: unidade lógico-aritmética
  //   f1 a f3: resultados do comparador (A > B, A = B, A < B, respectivamente)
endmodule

module ULA (
  input  p,
  input  [7:0] B,
  input  [7:0] A,
  output overflow,
  output f1,
  output f2,
  output [7:0] R,
  output f3
);

  comparador comparador_1 (.A(A), .B(B), .out_5(f2), .out_3(f1), .out_4(f3));
  aritmetica aritmetica_1 (.overflow(overflow), .A(A), .p(p), .B(B), .R(R));

  // Notes on the sheet:
  //   A, B: bytes de entrada
  //   s: pino seletor
  //   0 para soma
  //   1 para subtração
  //   f0: flag de overflow
  //   soma: somador
  //   comp: comparador
  //   R: byte resultado (saída)
  //   inv: módulo que inverte um byte
  //   f1 a f3: resultados do comparador (A > B, A = B, A < B, respectivamente)
endmodule

// aritm
module aritmetica (
  input  p,
  input  [7:0] B,
  input  [7:0] A,
  output overflow,
  output [7:0] R
);

  wire [7:0] inversor_1_complemento;

  inversor inversor_1 (.in(B), .p(p), .complemento(inversor_1_complemento));
  soma_8_bits soma_8_bits_1 (.o(overflow), .A(A), .B(inversor_1_complemento), .A_B(R), .in_3(p));

  // Notes on the sheet:
  //   A, B: bytes de entrada
  //   s: pino seletor
  //   0 para soma
  //   1 para subtração
  //   f0: flag de overflow
  //   soma: somador
  //   R: byte resultado (saída)
  //   inv: módulo que inverte um byte
  //   f1 a f3: resultados do comparador (A > B, A = B, A < B, respectivamente)
endmodule

// +
module soma_1_bit (
  input  a,
  input  b,
  input  cin,
  output cout,
  output s
);

  wire and_1_out, and_2_out, xor_2_out;

  or or_1 (cout, and_1_out, and_2_out);
  xor xor_1 (s, cin, xor_2_out);
  and and_1 (and_1_out, a, b);
  and and_2 (and_2_out, cin, xor_2_out);
  xor xor_2 (xor_2_out, a, b);

  // Notes on the sheet:
  //   Circuito somador de bits
  //   a, b: bits de entrada
  //   cin: carry de entrada
  //   cout: carry de saída
  //   s: bit soma (saída)
endmodule

// soma
module soma_8_bits (
  input  [7:0] B,
  input  [7:0] A,
  input  in_3,
  output o,
  output [7:0] A_B
);

  wire soma_1_bit_1_cout, soma_1_bit_2_cout, soma_1_bit_3_cout, soma_1_bit_4_cout, soma_1_bit_5_cout,
       soma_1_bit_6_cout, soma_1_bit_7_cout, soma_1_bit_8_cout;

  xor xor_1 (o, soma_1_bit_1_cout, soma_1_bit_2_cout);
  soma_1_bit soma_1_bit_1 (.cout(soma_1_bit_1_cout), .s(A_B[7]), .a(A[7]), .b(B[7]), .cin(soma_1_bit_2_cout));
  soma_1_bit soma_1_bit_2 (.cout(soma_1_bit_2_cout), .s(A_B[6]), .a(A[6]), .b(B[6]), .cin(soma_1_bit_3_cout));
  soma_1_bit soma_1_bit_3 (.cout(soma_1_bit_3_cout), .s(A_B[5]), .a(A[5]), .b(B[5]), .cin(soma_1_bit_4_cout));
  soma_1_bit soma_1_bit_4 (.cout(soma_1_bit_4_cout), .s(A_B[4]), .a(A[4]), .b(B[4]), .cin(soma_1_bit_5_cout));
  soma_1_bit soma_1_bit_5 (.cout(soma_1_bit_5_cout), .s(A_B[3]), .a(A[3]), .b(B[3]), .cin(soma_1_bit_6_cout));
  soma_1_bit soma_1_bit_6 (.cout(soma_1_bit_6_cout), .s(A_B[2]), .a(A[2]), .b(B[2]), .cin(soma_1_bit_7_cout));
  soma_1_bit soma_1_bit_7 (.cout(soma_1_bit_7_cout), .s(A_B[1]), .a(A[1]), .b(B[1]), .cin(soma_1_bit_8_cout));
  soma_1_bit soma_1_bit_8 (.cout(soma_1_bit_8_cout), .s(A_B[0]), .a(A[0]), .b(B[0]), .cin(in_3));

  // Notes on the sheet:
  //   o: flag de overflow
  //   A, B: bytes de entrada
  //   A + B: byte soma (saída)
  //   c0: carry de entrada
endmodule

// comp
module comparador (
  input  [7:0] A,
  input  [7:0] B,
  output out_3,
  output out_4,
  output out_5
);

  wire and_1_out, and_2_out, and_3_out, and_4_out, and_5_out, and_6_out, aritmetica_1_overflow,
       compara_1_bit_1_out_3, compara_1_bit_1_out_4, compara_1_bit_1_out_5, compara_com_0_1_out_2,
       compara_com_0_1_out_3, compara_com_0_1_out_4;
  wire [7:0] aritmetica_1_r;

  aritmetica aritmetica_1 (.overflow(aritmetica_1_overflow), .A(A), .p(1'b1), .B(B), .R(aritmetica_1_r));
  compara_com_0 compara_com_0_1 (
    .A(aritmetica_1_r), .out_2(compara_com_0_1_out_2), .out_3(compara_com_0_1_out_3),
    .out_4(compara_com_0_1_out_4));
  and and_1 (and_1_out, compara_com_0_1_out_3, ~aritmetica_1_overflow);  // AND_Gate
  and and_2 (and_2_out, compara_com_0_1_out_4, ~aritmetica_1_overflow);  // AND_Gate
  or or_1 (out_3, and_2_out, and_4_out);
  or or_2 (out_4, and_1_out, and_6_out);
  and and_3 (and_3_out, compara_com_0_1_out_2, ~aritmetica_1_overflow);  // AND_Gate
  or or_3 (out_5, and_3_out, and_5_out);
  and and_4 (and_4_out, aritmetica_1_overflow, compara_1_bit_1_out_3);
  and and_5 (and_5_out, aritmetica_1_overflow, compara_1_bit_1_out_4);
  compara_1_bit compara_1_bit_1 (
    .a(A[7]), .b(B[7]), .out_3(compara_1_bit_1_out_3), .out_4(compara_1_bit_1_out_4),
    .out_5(compara_1_bit_1_out_5));
  and and_6 (and_6_out, aritmetica_1_overflow, compara_1_bit_1_out_5);

  // Notes on the sheet:
  //   comp: comparador de dois bits
  //   cmp0: compara um byte com O
  //   cmp1: compara dois bits
  //   aritm: somador
  //   f1 a f3: resultados do comparador (A > B, A = B, A < B, respectivamente)
endmodule

// cmp0
module compara_com_0 (
  input  [7:0] A,
  output out_2,
  output out_3,
  output out_4
);

  wire not_1_out, not_2_out;

  not not_1 (not_1_out, A[7]);
  nor nor_1 (out_2, A[0], A[1], A[2], A[3], A[4], A[5], A[6], A[7]);
  not not_2 (not_2_out, out_2);
  and and_1 (out_4, not_2_out, not_1_out);

  assign out_3 = A[7];
endmodule

// cmp1
module compara_1_bit (
  input  a,
  input  b,
  output out_3,
  output out_4,
  output out_5
);

  wire not_1_out, not_2_out;

  not not_1 (not_1_out, a);
  and and_1 (out_3, not_1_out, b);
  nor nor_1 (out_4, out_3, out_5);
  not not_2 (not_2_out, b);
  and and_2 (out_5, a, not_2_out);

  // Notes on the sheet:
  //   a, b: bits de entrada
  //   f1 a f3: resultados do comparador (A > B, A = B, A < B, respectivamente)
endmodule

// inv
module inversor (
  input  [7:0] in,
  input  p,
  output [7:0] complemento
);

  xor xor_1 (complemento[0], p, in[0]);
  xor xor_2 (complemento[1], in[1], p);
  xor xor_3 (complemento[2], p, in[2]);
  xor xor_4 (complemento[3], p, in[3]);
  xor xor_5 (complemento[4], p, in[4]);
  xor xor_6 (complemento[5], in[5], p);
  xor xor_7 (complemento[6], in[6], p);
  xor xor_8 (complemento[7], in[7], p);

  // Notes on the sheet:
  //   Inversor de bits
  //   Tira o complemento de uma palavra de 8 bits
  //   in: entrada
  //   out: saída
  //   p: pino seletor
  //   quando 0, não afeta o resultado.
  //   quando 1, inverte os bits
endmodule
