// Logisim project somador.circ as structural Verilog: 2 circuits, main circuit main
module main (
  input  a,
  input  b,
  input  cin,
  output cout,
  output s
);

  wire and_1_out, and_2_out, xor_2_out;

  or or_1 (cout, and_1_out, and_2_out);
  xor xor_1 (s, cin, xor_2_out);
  and and_1 (and_1_out, a, b);
  and and_2 (and_2_out, cin, xor_2_out);
  xor xor_2 (xor_2_out, a, b);

  // Notes on the sheet:
  //   8569211
  //   2018.1
  //   Circuito somador de bits
  //   a, b: bits de entrada
  //   cin: carry de entrada
  //   cout: carry de saída
  //   s: bit soma (saída)
  //   Bruna Thalenberg
  //   MAC0329 - Álgebra Booleana
endmodule

module soma_4_bits (
  input  [3:0] A,
  input  [3:0] B,
  input  c0,
  output c4,
  output [3:0] A_B
);

  wire main_2_cout, main_3_cout, main_4_cout;

  main main_1 (.cout(c4), .s(A_B[3]), .a(A[3]), .b(B[3]), .cin(main_2_cout));
  main main_2 (.cout(main_2_cout), .s(A_B[2]), .a(A[2]), .b(B[2]), .cin(main_3_cout));
  main main_3 (.cout(main_3_cout), .s(A_B[1]), .a(A[1]), .b(B[1]), .cin(main_4_cout));
  main main_4 (.cout(main_4_cout), .s(A_B[0]), .a(A[0]), .b(B[0]), .cin(c0));
endmodule
