// Logisim project ep3a.circ as structural Verilog: 2 circuits, main circuit main
module main (
  input  [15:0] _1,
  input  _9,
  input  load,
  input  inc_1,
  input  reset_1,
  input  _0__destino_0___1__destino_1,
  input  write_0_read_1
);

  wire clock_1_out, not_1_out, not_2_out;
  wire [7:0] PC_q, ram_1_data, ram_1_data_2;
  wire [15:0] bit_extender_1_out, demultiplexer_1_out0, demultiplexer_1_out1, multiplexer_1_out,
       multiplexer_2_out;

  Clock clock_1 (.out(clock_1_out));
  Multiplexer #(.width(16)) multiplexer_1 (
    .in0(bit_extender_1_out), .in1(_1), .out(multiplexer_1_out), .sel(_9));  // open: en
  Counter PC (.load(load), .D(ram_1_data_2), .count(inc_1), .Q(PC_q), .clk(clock_1_out), .clr(reset_1));  // open: carry
  assign bit_extender_1_out = {{8{1'b0}}, PC_q};  // Bit_Extender bit_extender_1
  not not_1 (not_1_out, write_0_read_1);
  RAM #(.dataWidth(16), .bus("separate")) ram_1 (
    .addr(PC_q), .din(multiplexer_1_out), .data({ram_1_data_2, ram_1_data}), .str(not_1_out),
    .clk(clock_1_out), .ld(write_0_read_1));  // open: sel, clr
  Multiplexer #(.width(16)) multiplexer_2 (
    .in0({ram_1_data_2, ram_1_data}), .in1(multiplexer_1_out), .out(multiplexer_2_out), .sel(not_2_out));  // open: en
  Demultiplexer #(.width(16)) demultiplexer_1 (
    .out0(demultiplexer_1_out0), .out1(demultiplexer_1_out1), .in(multiplexer_2_out),
    .sel(_0__destino_0___1__destino_1), .en(_0__destino_0___1__destino_1));
  not not_2 (not_2_out, write_0_read_1);
  Hex_Digit_Display hex_digit_display_1 (.value(demultiplexer_1_out0[15:12]));  // open: dp
  Hex_Digit_Display hex_digit_display_2 (.value(demultiplexer_1_out1[15:12]));  // open: dp
  Hex_Digit_Display hex_digit_display_3 (.value(demultiplexer_1_out0[7:4]));  // open: dp
  Hex_Digit_Display hex_digit_display_4 (.value(demultiplexer_1_out0[11:8]));  // open: dp
  Hex_Digit_Display hex_digit_display_5 (.value(demultiplexer_1_out1[11:8]));  // open: dp
  Hex_Digit_Display hex_digit_display_6 (.value(demultiplexer_1_out1[7:4]));  // open: dp
  Hex_Digit_Display hex_digit_display_7 (.value(demultiplexer_1_out0[3:0]));  // open: dp
  Hex_Digit_Display hex_digit_display_8 (.value(demultiplexer_1_out1[3:0]));  // open: dp

  // Notes on the sheet:
  //   (6.)
  //   (2.) RAM
  //   (4.) DMUX
  //   (6.) Clock
  //   (8.) MUX
  //   (2.)
  //   (1.) pino de entrada (input)
  //   (3.) Contador de 8 bits (Program Counter)
  //   (7.) Pinos de controle diversos
  //   (10.) extensor 8->16 bits
  //   (8.)
  //   (10)
  //   (5.) Display de dígitos (que podem ser substituídos por pinos de saída)
  //   (9.) pino de controle de input: contador=0/input=1
  //   (8.)
  //   (4.)
  //   destino 0
  //   destino 1
  //   Projeto de Álgebra Booleana
  //   Arthur Massola
  //   Bruna Thalenberg
  //   (5.)
  //   (5.)
endmodule

module UC (
);

  wire [15:0] IR_q;

  Register #(.width(16)) IR (.Q(IR_q));  // open: D, en, clk, clr

  // Notes on the sheet:
  //   instrução
  //   operando
endmodule
