// Logisim project ep3b.circ as structural Verilog: 2 circuits, main circuit main
module main (
  input  in_count,
  input  load,
  input  inc_1,
  input  [15:0] in_4,
  output [7:0] out
);

  wire clk, not_1_out, r_w, reset;
  wire [7:0] PC_q;
  wire [15:0] bit_extender_1_out, data, multiplexer_1_out;

  Clock clock_1 (.out(clk));
  Multiplexer #(.width(16)) multiplexer_1 (
    .in0(bit_extender_1_out), .in1(in_4), .out(multiplexer_1_out), .sel(in_count));  // open: en
  Counter PC (.load(load), .D(data[7:0]), .count(inc_1), .Q(PC_q), .clk(clk), .clr(reset));  // open: carry
  assign bit_extender_1_out = {{8{1'b0}}, PC_q};  // Bit_Extender bit_extender_1
  not not_1 (not_1_out, r_w);
  RAM #(.dataWidth(16), .bus("separate")) ram_1 (
    .addr(PC_q), .din(multiplexer_1_out), .data(data), .str(not_1_out), .clk(clk), .ld(r_w));  // open: sel, clr
  UC uc_1 (.in(data), .r_w(r_w), .clk(clk), .reset(reset), .op(out));

  // Other names for the same wires on the sheet: in[15:0] = in_4

  // Notes on the sheet:
  //   (2)
  //   (1) RAM
  //   (2) Clock (clk)
  //   (3) MUX
  //   (4) extensor 8->16 bits
  //   (1)
  //   (3)
  //   (4)
  //   (5) pino de controle de input: contador=0/input=1
  //   in: input
  //   r/w: read = 1; write = 0.
  //   data: saída da RAM
  //   reset (autoexplicativo, reset = 1)
  //   mux1: saída do mux
  //   inc=1: modo de incremento do contador
  //   load: carregamento assíncrono do PC
  //   (PC) Contador de 8 bits (Program Counter)
  //   in/count: seta a fonte de entrada de dados para a RAM (0 = PC/1 = input)
  //   Projeto de Álgebra Booleana
  //   Arthur Massola
  //   Bruna Thalenberg
endmodule

module UC (
  input  [15:0] in,
  input  clk,
  output r_w,
  output [7:0] op,
  output reset
);

  wire _2_out, _7_out;
  wire [7:0] IR_q;

  Register #(.width(16)) IR (.D(in), .Q({IR_q, op}), .clk(clk));  // open: en, clr
  and _2 (_2_out, ~IR_q[0], IR_q[1], ~IR_q[2], ~IR_q[3], ~IR_q[4], ~IR_q[5], ~IR_q[6], ~IR_q[7]);  // AND_Gate
  and _7 (_7_out, IR_q[0], IR_q[1], IR_q[2], ~IR_q[3], ~IR_q[4], ~IR_q[5], ~IR_q[6], ~IR_q[7]);  // AND_Gate
  and _9 (reset, IR_q[0], ~IR_q[1], ~IR_q[2], IR_q[3], ~IR_q[4], ~IR_q[5], ~IR_q[6], ~IR_q[7]);  // AND_Gate
  and and_1 (r_w, ~_2_out, ~_7_out);  // AND_Gate
endmodule
