// Logisim project ep3c.circ as structural Verilog: 5 circuits, main circuit main
module main (
  input  [15:0] in_1,
  output [15:0] out
);

  wire and_1_out, clk, cp_ac, ee, jmp_1_jmp_4, load, not_1_out, not_2_out, r_w, reset, sub, uc_1_ac,
       uc_1_data, uc_1_jmp, uc_1_jmp_0, uc_1_jmp_0_2, uc_1_jmp_0_3;
  wire [7:0] multiplexer_1_out, op, PC_q;
  wire [15:0] ac, IR_q, multiplexer_2_out, multiplexer_3_out, res;

  and and_1 (and_1_out, ~ee, ~load);  // AND_Gate
  Clock clock_1 (.out(clk));
  Multiplexer #(.width(8)) multiplexer_1 (.in0(PC_q), .in1(op), .out(multiplexer_1_out), .sel(ee));  // open: en
  Counter PC (.load(load), .D(op), .count(and_1_out), .Q(PC_q), .clk(clk), .clr(reset));  // open: carry
  Multiplexer #(.width(16)) multiplexer_2 (.in0(ac), .in1(in_1), .out(multiplexer_2_out), .sel(cp_ac));  // open: en
  not not_1 (not_1_out, r_w);
  RAM #(.dataWidth(16), .bus("separate")) ram_1 (
    .addr(multiplexer_1_out), .din(multiplexer_2_out), .data(out), .str(not_1_out), .clk(clk), .ld(1'b1));  // open: sel, clr
  Register #(.width(16)) IR (.D(out), .en(1'b1), .Q(IR_q), .clk(clk));  // open: clr
  not not_2 (not_2_out, uc_1_data);
  Multiplexer #(.width(16)) multiplexer_3 (.in0(out), .in1(res), .out(multiplexer_3_out), .sel(not_2_out));  // open: en
  Register #(.width(16)) u_AC (.D(multiplexer_3_out), .en(uc_1_ac), .Q(ac), .clk(clk));  // open: clr
  aritm aritm_1 (.ee(out), .ac(ac), .out(res), .sub(sub));
  UC uc_1 (
    .in(IR_q), .reset(reset), .op(op), .data(uc_1_data), .jmp(uc_1_jmp), .jmp_0(uc_1_jmp_0),
    .jmp_0_2(uc_1_jmp_0_2), .jmp_0_3(uc_1_jmp_0_3), .out_15(sub), .cp_ac(cp_ac), .r_w(r_w), .ee(ee),
    .ac(uc_1_ac));  // open: out_13, prn, cp_in
  jmp jmp_1 (.ac(ac), .jmp(uc_1_jmp_0), .jmp_2(uc_1_jmp_0_3), .jmp_3(uc_1_jmp_0_2), .jmp_4(jmp_1_jmp_4));
  or or_1 (load, jmp_1_jmp_4, uc_1_jmp);

  // Other names for the same wires on the sheet: data[15:0] = out; in[15:0] = in_1

  // Notes on the sheet:
  //   (2)
  //   (1) RAM
  //   (2) Clock (clk)
  //   (PC) Contador de 8 bits (Program Counter)
  //   (UC) unidade de controle
  //   (IR) instruction register
  //   (ULA) unidade logico-aritmetica
  //   (JIF) subcircuito para verificação de JMP
  //   (1)
  //   (4)
  //   in: input
  //   ac: dado no AC
  //   r/w: read = 1; write = 0.
  //   data: saída da RAM
  //   reset (autoexplicativo, reset = 1)
  //   sub: flag para subtração na ULA
  //   res: resultado da operação na ULA
  //   ee: 1 quando deve-se deslocar para endereço em op
  //   cp ac: 1 quando deve-se copiar ac para a RAM
  //   op: endereço de memória (byte final da instrução)
  //   load: 1 quando deve-se realizar load assíncrono de op no PC
  //   Projeto de Álgebra Booleana
  //   Bruna Thalenberg
endmodule

module UC (
  input  [15:0] in,
  output cp_in,
  output r_w,
  output cp_ac,
  output reset,
  output data,
  output ee,
  output [7:0] op,
  output jmp,
  output jmp_0,
  output jmp_0_2,
  output jmp_0_3,
  output out_13,
  output ac,
  output out_15,
  output prn
);

  and _2 (cp_in, ~in[11], ~in[10], in[9], ~in[8]);  // AND_Gate
  and _7 (cp_ac, ~in[11], in[10], in[9], in[8]);  // AND_Gate
  and _9 (reset, in[11], ~in[10], ~in[9], in[8]);  // AND_Gate
  and _1 (data, ~in[11], ~in[10], ~in[9], in[8]);  // AND_Gate
  and _10 (jmp, in[11], ~in[10], in[9], ~in[8]);  // AND_Gate
  and _11 (jmp_0, in[11], ~in[10], in[9], in[8]);  // AND_Gate
  and _13 (jmp_0_2, in[11], in[10], ~in[9], in[8]);  // AND_Gate
  and _15 (jmp_0_3, in[11], in[10], in[9], in[8]);
  and _3 (out_13, ~in[11], ~in[10], in[9], in[8]);  // AND_Gate
  and _4 (out_15, ~in[11], in[10], ~in[9], ~in[8]);  // AND_Gate
  and _8 (prn, in[11], ~in[10], ~in[9], ~in[8]);  // AND_Gate
  and and_1 (r_w, ~cp_in, ~cp_ac);  // AND_Gate
  or or_1 (ee, cp_in, cp_ac, data, out_13, out_15, prn);
  or or_2 (ac, data, out_13, out_15);

  assign op = in[7:0];
endmodule

// JIF
module jmp (
  input  [15:0] ac,
  input  jmp,
  input  jmp_2,
  input  jmp_3,
  output jmp_4
);

  wire cmp0_1_out_2, cmp0_1_out_3, cmp0_1_out_4, jif_2_out, jif_3_out, jif_out;

  cmp0 cmp0_1 (.A(ac), .out_2(cmp0_1_out_2), .out_3(cmp0_1_out_3), .out_4(cmp0_1_out_4));
  and jif (jif_out, cmp0_1_out_3, jmp_2);
  and jif_2 (jif_2_out, cmp0_1_out_4, jmp);
  or or_1 (jmp_4, jif_2_out, jif_out, jif_3_out);
  and jif_3 (jif_3_out, cmp0_1_out_2, jmp_3);
endmodule

module cmp0 (
  input  [15:0] A,
  output out_2,
  output out_3,
  output out_4
);

  wire not_1_out, not_2_out;

  not not_1 (not_1_out, A[7]);
  nor nor_1 (out_2, A[0], A[1], A[2], A[3], A[4], A[5], A[6], A[7]);
  not not_2 (not_2_out, out_2);
  and and_1 (out_4, not_2_out, not_1_out);

  assign out_3 = A[7];
endmodule

// ULA
module aritm (
  input  sub,
  input  [15:0] ee,
  input  [15:0] ac,
  output [15:0] out
);

  wire [7:0] aritmetica_1_r, bit_extender_1_out, bit_extender_2_out;

  Bit_Extender #(.in_width(16), .out_width(8)) bit_extender_1 (.in(ee), .out(bit_extender_1_out));
  Bit_Extender #(.in_width(16), .out_width(8)) bit_extender_2 (.in(ac), .out(bit_extender_2_out));
  aritmetica aritmetica_1 (
    .A(bit_extender_2_out), .p(sub), .B(bit_extender_1_out), .R(aritmetica_1_r));  // open: overflow
  assign out = {{8{1'b0}}, aritmetica_1_r};  // Bit_Extender bit_extender_3
endmodule
